# Fritzing sketch Untitled Sketch (saved by Fritzing 0.9.5d)
breadboards: 1

parts:
  LED1 = LED - 5mm [color="Red (633nm)" package="5 mm [THT]"]
  LED2 = LED - 5mm [color="Red (633nm)" package="5 mm [THT]"]
  LED4 = LED - 5mm [color="Red (633nm)" package="5 mm [THT]"]
  M1 = STM32F103C8T6 blue mini board
  LED5 = LED - 5mm [color="Red (633nm)" package="5 mm [THT]"]
  R1 = Resistor [tolerance=±5% resistance=220 package="0402 [SMD]"]
  R2 = Resistor [tolerance=±5% resistance=220 package="0402 [SMD]"]
  R3 = Resistor [tolerance=±5% resistance=220 package="0402 [SMD]"]
  R4 = Resistor [tolerance=±5% resistance=220 package="0402 [SMD]"]

nets:
  N1: LED1.cathode, R4.Pin_0
  N2: LED1.anode, M1.A4
  N3: LED2.cathode, R3.Pin_0
  N4: LED2.anode, M1.A3
  N5: LED4.cathode, R1.Pin_0
  N6: LED4.anode, M1.A1
  N7: M1.G, R1.Pin_1, R2.Pin_1, R3.Pin_1, R4.Pin_1
  N8: M1.A2, LED5.anode
  N9: LED5.cathode, R2.Pin_0
