# Fritzing sketch Untitled Sketch (saved by Fritzing 0.9.5d)
breadboards: 1

parts:
  M1 = STM32F103C8T6 blue mini board
  LED1 = LED - 5mm [color="Red (633nm)" package="5 mm [THT]"]
  R1 = Resistor [tolerance=±5% resistance=220 package="0805 [SMD]"]
  S1 = Square Pushbutton
  S2 = Square Pushbutton

nets:
  N1: M1.G, M1.GND, R1.Pin_1, S1.leg0, S2.leg0
  N2: M1.A0, LED1.anode
  N3: M1.A1, S2.leg1
  N4: M1.A2, S1.leg1
  N5: LED1.cathode, R1.Pin_0
