# Fritzing sketch Untitled Sketch (saved by Fritzing 0.9.5d)
breadboards: 1

parts:
  M1 = STM32F103C8T6 blue mini board
  LED1 = smd LED [color="Red (633nm)" package="0603 [SMD]"]
  S1 = Square Pushbutton
  R1 = Resistor [tolerance=±5% resistance=220 package="0402 [SMD]"]

nets:
  N1: M1.G, S1.leg0, R1.Pin_1
  N2: M1.A0, LED1.anode
  N3: M1.A1, S1.leg1
  N4: LED1.cathode, R1.Pin_0
