# Fritzing sketch Untitled Sketch (saved by Fritzing 0.9.5d)
breadboards: 2

parts:
  M1 = STM32F103C8T6 blue mini board
  LED1 = LED - 5mm [color="Red (633nm)" package="5 mm [THT]"]
  LED2 = LED - 5mm [color="Red (633nm)" package="5 mm [THT]"]
  LED3 = LED - 5mm [color="Red (633nm)" package="5 mm [THT]"]
  LED4 = LED - 5mm [color="Red (633nm)" package="5 mm [THT]"]
  R2 = Resistor [tolerance=±5% resistance=220 package="0603 [SMD]"]
  R3 = Resistor [tolerance=±5% resistance=220 package="0603 [SMD]"]
  R4 = Resistor [tolerance=±5% resistance=220 package="0603 [SMD]"]
  R5 = Resistor [tolerance=±5% resistance=220 package="0603 [SMD]"]
  S1 = Square Pushbutton
  S2 = Square Pushbutton
  S3 = Square Pushbutton
  S4 = Square Pushbutton

nets:
  N1: M1.B4, S4.leg1
  N2: M1.B5, S3.leg1
  N3: M1.B6, S2.leg1
  N4: M1.B7, S1.leg1
  N5: M1.G, R2.Pin_1, R3.Pin_1, R4.Pin_1, R5.Pin_1, S1.leg0, S2.leg0, S3.leg0, S4.leg0
  N6: M1.A4, LED4.cathode
  N7: M1.A5, LED3.cathode
  N8: M1.A6, LED2.cathode
  N9: M1.A7, LED1.cathode
  N10: LED1.anode, R5.Pin_0
  N11: LED2.anode, R4.Pin_0
  N12: LED3.anode, R3.Pin_0
  N13: LED4.anode, R2.Pin_0
