# Fritzing sketch Untitled Sketch (saved by Fritzing 0.9.5d)
breadboards: 1

parts:
  DI1 = 7-Segment LED Display [package=THT]
  M1 = STM32F103C8T6 blue mini board
  S1 = Square Pushbutton
  S2 = Square Pushbutton

nets:
  N1: DI1.cathodeD, M1.A3
  N2: DI1.commAnode, M1.3.3V, M1.3.3
  N3: DI1.cathodeC, M1.A2
  N4: M1.G, S1.leg0, S2.leg0
  N5: M1.B0, S1.leg1
  N6: M1.B1, S2.leg1
