# Fritzing sketch Untitled Sketch (saved by Fritzing 0.9.5d)
breadboards: 2

parts:
  M1 = STM32F103C8T6 blue mini board
  Nano1 = Arduino Nano v2.3
  J1 = Basic Servo
  S1 = Square Pushbutton
  S2 = Square Pushbutton

nets:
  GND: M1.G, M1.GND, Nano1.GND, J1.gnd, S1.leg0, S2.leg0
  N1: M1.A6, J1.vcc, J1.pulse
