# Fritzing sketch Untitled Sketch (saved by Fritzing 0.9.5d)
breadboards: 1

parts:
  M1 = STM32F103C8T6 blue mini board
  U2 = ESP8266 WiFi Module [part_number=ESP8266]
  R1 = PHOTOCELL [package=photocell-kit]
  R2 = Resistor [tolerance=±5% resistance=220 package="2512 [SMD]"]

nets:
  N1: M1.A9, U2.RX
  N2: M1.A10, U2.TX
  N3: M1.G, M1.GND, U2.GND#23, R2.Pin_0
  N4: M1.3.3V, R1.P$2
  N5: M1.A0, R1.P$1, R2.Pin_1
  N6: U2.IO2, U2.D2, U2.CLK, U2.CMD, U2.D0
  N7: U2.IO4, U2.3.3V
  N8: U2.GND#12, U2.GND#13, U2.IO5
  N9: U2.CHIP_EN, U2.XPD, U2.IO14, U2.IO12, U2.IO13
